# Fritzing sketch Untitled Sketch (saved by Fritzing 0.9.3b)

parts:
  Част1 = Arduino Uno (Rev3)
  BT1 = Bluetooth HC-06u [package=THT]
  KF-1 = KF-301 Relay [package=THT]
  L1 = Solenoid
  VCC1 = Battery block 9V

nets:
  N1: Част1.D8, KF-1.signal
  N2: Част1.D0/RX, BT1.TXD
  N3: Част1.D1/TX, BT1.RXD
  3V3: Част1.3V3, BT1.VCC
  N4: Част1.5V, KF-1.power
  GND: Част1.GND, BT1.GND, KF-1.ground
  N5: KF-1.C, VCC1.+
  N6: KF-1.NO, L1.pin2

custom parts:
  Bluetooth HC-06u: Bluetooth HC-06 - face up, pins down 16.5mm x 37.5mm PCB
  KF-301 Relay: KF-301
